// Logisim project 8bit_cpu_v2.circ as structural Verilog: 18 circuits, main circuit main
module main (
  input  RUN,
  input  CLK,
  input  Reset,
  input  INT,
  output [7:0] out_5,
  output [7:0] out_6
);

  wire and_1_out, and_2_out, int_enable_1_q, int_pending_1_q;
  wire [1:0] alu_1_zero;
  wire [6:0] keyboard_1_data;
  wire [7:0] alu_1_result, controlled_buffer_1_out, DIGIT_result, instruction_register_1_ir_out, MAR_result,
       multiplexer_1_out, multiplexer_2_out, multiplexer_3_out, Operand_Register_result,
       Output_Register_result, program_counter_1_result, ram_1_dout, Register_B_result, rom_1_data,
       shifter_1_out, TEMP1_result, TEMP2_result, TEMP3_result, TEMP_result;
  wire [8:0] micro_program_counter_1_result;
  wire [63:0] rom_2_data;

  ROM rom_1 (.addr(program_counter_1_result), .data(rom_1_data));
  INT_Enable int_enable_1 (.RESET(Reset), .EN(rom_2_data[58]), .CLK(CLK), .D(rom_2_data[59]), .Q(int_enable_1_q));
  INT_Pending int_pending_1 (.CLK(CLK), .En(1'b1), .D(INT), .CLR(rom_2_data[60]), .Q(int_pending_1_q));
  Program_Counter program_counter_1 (
    .En(rom_2_data[0]), .CLK(and_1_out), .D(controlled_buffer_1_out), .S0(rom_2_data[7]), .S1(rom_2_data[8]),
    .Result(program_counter_1_result));
  assign controlled_buffer_1_out = rom_2_data[3] ? instruction_register_1_ir_out : 8'bz;  // Controlled_Buffer controlled_buffer_1
  Instruction_Register instruction_register_1 (
    .Load(rom_2_data[5]), .CLK(and_1_out), .data_in(rom_1_data), .ir_out(instruction_register_1_ir_out));
  Register_8bit Operand_Register (
    .EN(rom_2_data[56]), .CLK(and_1_out), .D(rom_1_data), .Result(Operand_Register_result));
  and and_1 (and_1_out, RUN, CLK);
  and and_2 (and_2_out, int_enable_1_q, int_pending_1_q);
  ROM #(.addrWidth(9), .dataWidth(64)) rom_2 (.addr(micro_program_counter_1_result), .data(rom_2_data));
  Micro_Program_Counter micro_program_counter_1 (
    .En(RUN), .CLK(CLK), .OPCODE(instruction_register_1_ir_out[7:4]), .Branch_Target(rom_2_data[24:16]),
    .MUX_in(rom_2_data[26:25]), .Branch_OP(rom_2_data[29:27]), .OPERAND(instruction_register_1_ir_out[3:0]),
    .KBD_val(keyboard_1_data), .is_C(alu_1_zero[1]), .is_Z(alu_1_zero[0]), .INT_request(and_2_out),
    .Result(micro_program_counter_1_result));
  assign controlled_buffer_1_out = rom_2_data[1] ? program_counter_1_result : 8'bz;  // Controlled_Buffer controlled_buffer_2
  Multiplexer #(.select(2), .width(8)) multiplexer_1 (
    .in0(Operand_Register_result), .in1(out_5), .in2(program_counter_1_result), .out(multiplexer_1_out),
    .sel(rom_2_data[54:53]));  // open: in3
  RAM ram_1 (
    .addr(MAR_result), .we(rom_2_data[9]), .oe(rom_2_data[10]), .clk(CLK), .din(controlled_buffer_1_out),
    .dout(ram_1_dout));
  LedBar LED_output (
    .led0(Output_Register_result[7]), .led1(Output_Register_result[6]), .led2(Output_Register_result[5]),
    .led3(Output_Register_result[4]), .led4(Output_Register_result[3]), .led5(Output_Register_result[2]),
    .led6(Output_Register_result[1]), .led7(Output_Register_result[0]));
  Stack_Pointer stack_pointer_1 (
    .RESET(Reset), .En(rom_2_data[48]), .CLK(CLK), .Inc(rom_2_data[50]), .D(controlled_buffer_1_out),
    .S0(rom_2_data[51]), .S1(rom_2_data[52]), .Result(out_5));
  assign controlled_buffer_1_out = rom_2_data[49] ? out_5 : 8'bz;  // Controlled_Buffer controlled_buffer_3
  Register_8bit MAR (.EN(rom_2_data[55]), .CLK(CLK), .D(multiplexer_1_out), .Result(MAR_result));
  Register_8bit_with_clear Register_A (
    .EN(rom_2_data[6]), .CLK(CLK), .D(controlled_buffer_1_out), .CLR(rom_2_data[44]), .Result(out_6));
  Register_8bit Register_B (.EN(rom_2_data[14]), .CLK(CLK), .D(controlled_buffer_1_out), .Result(Register_B_result));
  Register_8bit Output_Register (
    .EN(rom_2_data[11]), .CLK(CLK), .D(controlled_buffer_1_out), .Result(Output_Register_result));
  assign controlled_buffer_1_out = rom_2_data[57] ? ram_1_dout : 8'bz;  // Controlled_Buffer controlled_buffer_4
  assign controlled_buffer_1_out = rom_2_data[4] ? shifter_1_out : 8'bz;  // Controlled_Buffer controlled_buffer_5
  Shifter shifter_1 (.in(out_6), .\dist (rom_2_data[47:45]), .out(shifter_1_out));
  Multiplexer #(.width(8)) multiplexer_2 (
    .in0(shifter_1_out), .in1(controlled_buffer_1_out), .out(multiplexer_2_out), .sel(rom_2_data[42]));
  Multiplexer #(.width(8)) multiplexer_3 (
    .in0(Register_B_result), .in1(8'h30), .out(multiplexer_3_out), .sel(rom_2_data[43]));
  Keyboard #(.buflen(8)) keyboard_1 (
    .clk(CLK), .re(rom_2_data[40]), .clr(rom_2_data[41]), .data(keyboard_1_data));  // open: avail
  assign controlled_buffer_1_out = rom_2_data[40] ? {1'b0, keyboard_1_data} : 8'bz;  // Controlled_Buffer controlled_buffer_6
  Register_8bit TEMP (.EN(rom_2_data[30]), .CLK(CLK), .D(controlled_buffer_1_out), .Result(TEMP_result));
  Register_8bit DIGIT (.EN(rom_2_data[32]), .CLK(CLK), .D(controlled_buffer_1_out), .Result(DIGIT_result));
  Register_8bit TEMP1 (.EN(rom_2_data[34]), .CLK(CLK), .D(controlled_buffer_1_out), .Result(TEMP1_result));
  Register_8bit TEMP2 (.EN(rom_2_data[36]), .CLK(CLK), .D(controlled_buffer_1_out), .Result(TEMP2_result));
  assign controlled_buffer_1_out = rom_2_data[39] ? TEMP3_result : 8'bz;  // Controlled_Buffer controlled_buffer_7
  Register_8bit TEMP3 (.EN(rom_2_data[38]), .CLK(CLK), .D(controlled_buffer_1_out), .Result(TEMP3_result));
  ALU alu_1 (
    .A(multiplexer_2_out), .B(multiplexer_3_out), .CLK(CLK), .flag_EN(rom_2_data[61]), .EN(rom_2_data[15]),
    .S0(rom_2_data[12]), .S1(rom_2_data[13]), .flag_data(controlled_buffer_1_out), .flag_op(rom_2_data[63]),
    .Carry(alu_1_zero[1]), .Zero(alu_1_zero[0]), .Result(alu_1_result));
  assign controlled_buffer_1_out = rom_2_data[2] ? alu_1_result : 8'bz;  // Controlled_Buffer controlled_buffer_8
  assign controlled_buffer_1_out = rom_2_data[31] ? TEMP_result : 8'bz;  // Controlled_Buffer controlled_buffer_9
  assign controlled_buffer_1_out = rom_2_data[33] ? DIGIT_result : 8'bz;  // Controlled_Buffer controlled_buffer_10
  assign controlled_buffer_1_out = rom_2_data[35] ? TEMP1_result : 8'bz;  // Controlled_Buffer controlled_buffer_11
  assign controlled_buffer_1_out = rom_2_data[37] ? TEMP2_result : 8'bz;  // Controlled_Buffer controlled_buffer_12
  assign controlled_buffer_1_out = rom_2_data[62] ? {{6{1'b0}}, alu_1_zero} : 8'bz;  // Controlled_Buffer controlled_buffer_13

  // Notes on the sheet:
  //   contents of rom_1 (hex, n*v repeats v):
  //   10 0 30 1 20 0 10 2 40 3 c0 0 1e 40 5 c0 23 d0 1b 10 9 2f 10 6 2f e0 c 10 9 2f 10 7 2f e0 c 10 9 2f
  //   10 8 2f f0 9*0 f0 188*0 10 0 20 5 10 4 20 3 a0
  //   contents of rom_2 (hex, n*v repeats v):
  //   2e700000 21 2000000 29*0 1e260000 3e330000 100000000000001 80000000000000 408 200000004000040
  //   100000000000 10066000000 c0080009000 100000004 600400000010 201000000010 800004000 42000008000
  //   4000000004 8000004000 40200008000 44 6270000 10004000040 12*0 36440000 100000000000001
  //   80000000000000 4000210 4000810 27*0 100000000000001 80000000000000 408 200000000004000
  //   2000000000008000 4000044 10*0 1400000000000000 1000000000000 a0000000000000 283 1000000000000
  //   a0000000000000 210 1000000000000 a0000000000000 4000000004000200 6*0 100000000000001 80000000000000
  //   408 200000000004000 2000000000009000 4000044 26*0 1000000000000 a0000000000000 4000210 29*0
  //   a0000000000000 440 205000004000040 29*0 1000000000000 a0000000000000 21 202 7c10000 27*0
  //   a0000000000000 400 200000000000101 5000004000000 28*0 4000000 31*0 a0000000000000 400
  //   a205000000000000 a0000000000000 400 205000000000040 a0000000000000 400 e05000004000101 23*0
  //   c00000004000000 31*0 fc00000 4000001 30*0 17c00000 4000001 30*0 21 4000109 30*0 7e00000
endmodule

module ALU_firstBit (
  input  A,
  input  B,
  input  Mode,
  output OR_Out,
  output AND_Out,
  output Cout,
  output Sum
);

  wire and_2_out, and_3_out, xor_1_out, xor_2_out;

  xor xor_1 (xor_1_out, B, Mode);
  or or_1 (OR_Out, A, B);
  and and_1 (AND_Out, A, B);
  and and_2 (and_2_out, A, xor_1_out);
  xor xor_2 (xor_2_out, A, xor_1_out);
  and and_3 (and_3_out, Mode, xor_2_out);
  xor xor_3 (Sum, xor_2_out, Mode);
  or or_2 (Cout, and_2_out, and_3_out);
endmodule

module ALU_otherBit (
  input  A,
  input  B,
  input  Mode,
  input  Cin,
  output OR_Out,
  output AND_Out,
  output Cout,
  output Sum
);

  wire and_2_out, and_3_out, xor_1_out, xor_2_out;

  xor xor_1 (xor_1_out, B, Mode);
  or or_1 (OR_Out, A, B);
  and and_1 (AND_Out, A, B);
  and and_2 (and_2_out, A, xor_1_out);
  xor xor_2 (xor_2_out, A, xor_1_out);
  or or_2 (Cout, and_2_out, and_3_out);
  and and_3 (and_3_out, Cin, xor_2_out);
  xor xor_3 (Sum, xor_2_out, Cin);
endmodule

module ALU (
  input  [7:0] A,
  input  [7:0] B,
  input  CLK,
  input  flag_EN,
  input  EN,
  input  S0,
  input  S1,
  input  [7:0] flag_data,
  input  flag_op,
  output Carry,
  output Zero,
  output [7:0] Result
);

  wire alu_firstbit_1_cout, alu_otherbit_1_cout, alu_otherbit_2_cout, alu_otherbit_3_cout,
       alu_otherbit_4_cout, alu_otherbit_5_cout, alu_otherbit_6_cout, alu_otherbit_7_cout, multiplexer_2_out,
       multiplexer_3_out, nor_1_out;
  wire [7:0] alu_firstbit_1_and_out, alu_firstbit_1_or_out, alu_firstbit_1_sum, multiplexer_1_out;

  ALU_firstBit alu_firstbit_1 (
    .A(A[0]), .B(B[0]), .Mode(S0), .OR_Out(alu_firstbit_1_or_out[0]), .AND_Out(alu_firstbit_1_and_out[0]),
    .Sum(alu_firstbit_1_sum[0]), .Cout(alu_firstbit_1_cout));
  ALU_otherBit alu_otherbit_1 (
    .A(A[1]), .B(B[1]), .Mode(S0), .Cin(alu_firstbit_1_cout), .AND_Out(alu_firstbit_1_and_out[1]),
    .OR_Out(alu_firstbit_1_or_out[1]), .Sum(alu_firstbit_1_sum[1]), .Cout(alu_otherbit_1_cout));
  ALU_otherBit alu_otherbit_2 (
    .A(A[2]), .B(B[2]), .Mode(S0), .Cin(alu_otherbit_1_cout), .AND_Out(alu_firstbit_1_and_out[2]),
    .OR_Out(alu_firstbit_1_or_out[2]), .Sum(alu_firstbit_1_sum[2]), .Cout(alu_otherbit_2_cout));
  ALU_otherBit alu_otherbit_3 (
    .A(A[3]), .B(B[3]), .Mode(S0), .Cin(alu_otherbit_2_cout), .AND_Out(alu_firstbit_1_and_out[3]),
    .OR_Out(alu_firstbit_1_or_out[3]), .Sum(alu_firstbit_1_sum[3]), .Cout(alu_otherbit_3_cout));
  ALU_otherBit alu_otherbit_4 (
    .A(A[4]), .B(B[4]), .Mode(S0), .Cin(alu_otherbit_3_cout), .AND_Out(alu_firstbit_1_and_out[4]),
    .OR_Out(alu_firstbit_1_or_out[4]), .Sum(alu_firstbit_1_sum[4]), .Cout(alu_otherbit_4_cout));
  ALU_otherBit alu_otherbit_5 (
    .A(A[5]), .B(B[5]), .Mode(S0), .Cin(alu_otherbit_4_cout), .AND_Out(alu_firstbit_1_and_out[5]),
    .OR_Out(alu_firstbit_1_or_out[5]), .Sum(alu_firstbit_1_sum[5]), .Cout(alu_otherbit_5_cout));
  ALU_otherBit alu_otherbit_6 (
    .A(A[6]), .B(B[6]), .Mode(S0), .Cin(alu_otherbit_5_cout), .AND_Out(alu_firstbit_1_and_out[6]),
    .OR_Out(alu_firstbit_1_or_out[6]), .Sum(alu_firstbit_1_sum[6]), .Cout(alu_otherbit_6_cout));
  ALU_otherBit alu_otherbit_7 (
    .A(A[7]), .B(B[7]), .Mode(S0), .Cin(alu_otherbit_6_cout), .AND_Out(alu_firstbit_1_and_out[7]),
    .OR_Out(alu_firstbit_1_or_out[7]), .Sum(alu_firstbit_1_sum[7]), .Cout(alu_otherbit_7_cout));
  Multiplexer #(.select(2), .width(8)) multiplexer_1 (
    .in0(alu_firstbit_1_sum), .in1(alu_firstbit_1_sum), .in2(alu_firstbit_1_or_out),
    .in3(alu_firstbit_1_and_out), .out(multiplexer_1_out), .sel({S1, S0}));
  nor nor_1 (nor_1_out, multiplexer_1_out[0], multiplexer_1_out[1], multiplexer_1_out[2], multiplexer_1_out[3], multiplexer_1_out[4], multiplexer_1_out[5], multiplexer_1_out[6], multiplexer_1_out[7]);
  Multiplexer multiplexer_2 (.in0(alu_otherbit_7_cout), .in1(flag_data[1]), .out(multiplexer_2_out), .sel(flag_op));
  Multiplexer multiplexer_3 (.in0(nor_1_out), .in1(flag_data[0]), .out(multiplexer_3_out), .sel(flag_op));
  Register_1bit register_1bit_1 (.D(multiplexer_2_out), .En(flag_EN), .CLK(CLK), .Q(Carry));
  Register_1bit register_1bit_2 (.D(multiplexer_3_out), .En(flag_EN), .CLK(CLK), .Q(Zero));
  Register_8bit register_8bit_1 (.EN(EN), .CLK(CLK), .D(multiplexer_1_out), .Result(Result));
endmodule

module Register_1bit (
  input  D,
  input  En,
  input  CLK,
  output Q
);

  wire and_1_out, and_2_out, not_1_out, or_1_out;

  not not_1 (not_1_out, En);
  and and_1 (and_1_out, D, En);
  and and_2 (and_2_out, not_1_out, Q);
  or or_1 (or_1_out, and_1_out, and_2_out);
  D_Flip_Flop d_ff_1 (.D(or_1_out), .clk(CLK), .Q(Q));  // open: Qn, preset, reset
endmodule

module Register_8bit (
  input  EN,
  input  CLK,
  input  [7:0] D,
  output [7:0] Result
);

  Register_1bit register_1bit_1 (.D(D[0]), .En(EN), .CLK(CLK), .Q(Result[0]));
  Register_1bit register_1bit_2 (.D(D[1]), .En(EN), .CLK(CLK), .Q(Result[1]));
  Register_1bit register_1bit_3 (.D(D[2]), .En(EN), .CLK(CLK), .Q(Result[2]));
  Register_1bit register_1bit_4 (.D(D[3]), .En(EN), .CLK(CLK), .Q(Result[3]));
  Register_1bit register_1bit_5 (.D(D[4]), .En(EN), .CLK(CLK), .Q(Result[4]));
  Register_1bit register_1bit_6 (.D(D[5]), .En(EN), .CLK(CLK), .Q(Result[5]));
  Register_1bit register_1bit_7 (.D(D[6]), .En(EN), .CLK(CLK), .Q(Result[6]));
  Register_1bit register_1bit_8 (.D(D[7]), .En(EN), .CLK(CLK), .Q(Result[7]));
endmodule

module Program_Counter (
  input  En,
  input  CLK,
  input  [7:0] D,
  input  S0,
  input  S1,
  output [7:0] Result
);

  wire [7:0] increment_decrement_8bit_1_result, multiplexer_1_out;

  Increment_Decrement_8bit increment_decrement_8bit_1 (
    .A(Result), .Mode(1'b0), .Result(increment_decrement_8bit_1_result));
  Multiplexer #(.select(2), .width(8)) multiplexer_1 (
    .in0(increment_decrement_8bit_1_result), .in1(8'hf0), .in2(D), .in3({8{1'b0}}), .out(multiplexer_1_out),
    .sel({S1, S0}));
  Register_8bit register_8bit_1 (.EN(En), .CLK(CLK), .D(multiplexer_1_out), .Result(Result));
endmodule

module Increment_Decrement_8bit (
  input  [7:0] A,
  input  Mode,
  output [7:0] Result
);

  wire add_sub_firstbit_1_cout, add_sub_otherbit_1_cout, add_sub_otherbit_2_cout, add_sub_otherbit_3_cout,
       add_sub_otherbit_4_cout, add_sub_otherbit_5_cout, add_sub_otherbit_6_cout;

  Add_Sub_firstBit add_sub_firstbit_1 (
    .A(A[0]), .B(1'b1), .Mode(Mode), .Sum(Result[0]), .Cout(add_sub_firstbit_1_cout));
  Add_Sub_otherBit add_sub_otherbit_1 (
    .A(A[1]), .B(1'b0), .Mode(Mode), .Cin(add_sub_firstbit_1_cout), .Sum(Result[1]),
    .Cout(add_sub_otherbit_1_cout));
  Add_Sub_otherBit add_sub_otherbit_2 (
    .A(A[2]), .B(1'b0), .Mode(Mode), .Cin(add_sub_otherbit_1_cout), .Sum(Result[2]),
    .Cout(add_sub_otherbit_2_cout));
  Add_Sub_otherBit add_sub_otherbit_3 (
    .A(A[3]), .B(1'b0), .Mode(Mode), .Cin(add_sub_otherbit_2_cout), .Sum(Result[3]),
    .Cout(add_sub_otherbit_3_cout));
  Add_Sub_otherBit add_sub_otherbit_4 (
    .A(A[4]), .B(1'b0), .Mode(Mode), .Cin(add_sub_otherbit_3_cout), .Sum(Result[4]),
    .Cout(add_sub_otherbit_4_cout));
  Add_Sub_otherBit add_sub_otherbit_5 (
    .A(A[5]), .B(1'b0), .Mode(Mode), .Cin(add_sub_otherbit_4_cout), .Sum(Result[5]),
    .Cout(add_sub_otherbit_5_cout));
  Add_Sub_otherBit add_sub_otherbit_6 (
    .A(A[6]), .B(1'b0), .Mode(Mode), .Cin(add_sub_otherbit_5_cout), .Sum(Result[6]),
    .Cout(add_sub_otherbit_6_cout));
  Add_Sub_otherBit add_sub_otherbit_7 (
    .A(A[7]), .B(Mode), .Mode(1'b0), .Cin(add_sub_otherbit_6_cout), .Sum(Result[7]));  // open: Cout
endmodule

module Add_Sub_firstBit (
  input  A,
  input  B,
  input  Mode,
  output Cout,
  output Sum
);

  wire and_1_out, and_2_out, xor_1_out, xor_2_out;

  xor xor_1 (xor_1_out, B, Mode);
  and and_1 (and_1_out, A, xor_1_out);
  xor xor_2 (xor_2_out, A, xor_1_out);
  and and_2 (and_2_out, Mode, xor_2_out);
  xor xor_3 (Sum, xor_2_out, Mode);
  or or_1 (Cout, and_1_out, and_2_out);
endmodule

module Instruction_Register (
  input  Load,
  input  CLK,
  input  [7:0] data_in,
  output [7:0] ir_out
);

  Register_8bit register_8bit_1 (.EN(Load), .CLK(CLK), .D(data_in), .Result(ir_out));
endmodule

module Micro_Program_Counter (
  input  En,
  input  CLK,
  input  [3:0] OPCODE,
  input  [8:0] Branch_Target,
  input  [1:0] MUX_in,
  input  [2:0] Branch_OP,
  input  [3:0] OPERAND,
  input  [6:0] KBD_val,
  input  is_C,
  input  is_Z,
  input  INT_request,
  output [8:0] Result
);

  wire and_1_out, and_2_out, and_3_out, and_4_out, and_5_out, and_6_out, comparator_1_eq, comparator_1_gt,
       comparator_2_lt, multiplexer_2_out, not_1_out, not_2_out, not_3_out, not_4_out, not_5_out, not_6_out,
       not_7_out, not_8_out, not_9_out, not_10_out, not_11_out, not_12_out, not_13_out, or_1_out;
  wire [8:0] increment_decrement_9bit_1_result, multiplexer_1_out, multiplexer_3_out;

  and and_1 (and_1_out, not_1_out, not_2_out, not_3_out, OPCODE[0], OPERAND[3], OPERAND[2], OPERAND[1], not_7_out);
  not not_1 (not_1_out, OPCODE[3]);
  not not_2 (not_2_out, OPCODE[2]);
  not not_3 (not_3_out, OPCODE[1]);
  and and_2 (and_2_out, not_4_out, not_5_out, OPCODE[1], not_6_out, OPERAND[3], OPERAND[2], OPERAND[1], OPERAND[0]);
  not not_4 (not_4_out, OPCODE[3]);
  not not_5 (not_5_out, OPCODE[2]);
  not not_6 (not_6_out, OPCODE[0]);
  not not_7 (not_7_out, OPERAND[0]);
  not not_8 (not_8_out, OPCODE[3]);
  not not_9 (not_9_out, OPCODE[2]);
  not not_10 (not_10_out, OPCODE[1]);
  and and_3 (and_3_out, not_8_out, not_9_out, not_10_out, OPCODE[0], OPERAND[3], OPERAND[2], not_11_out, OPERAND[0]);
  not not_11 (not_11_out, OPERAND[1]);
  Increment_Decrement_9bit increment_decrement_9bit_1 (
    .A(Result), .Mode(1'b0), .Result(increment_decrement_9bit_1_result));
  Multiplexer #(.width(9)) multiplexer_1 (
    .in0(increment_decrement_9bit_1_result), .in1(Branch_Target), .out(multiplexer_1_out),
    .sel(multiplexer_2_out));
  Multiplexer #(.select(3)) multiplexer_2 (
    .in0(1'b1), .in1(is_Z), .in2(is_C), .in3(and_1_out), .in4(not_12_out), .in5(INT_request),
    .in6(and_2_out), .in7(and_3_out), .out(multiplexer_2_out), .sel(Branch_OP));
  not not_12 (not_12_out, and_4_out);
  and and_4 (and_4_out, and_5_out, and_6_out);
  and and_5 (and_5_out, not_13_out, KBD_val[5], KBD_val[4]);
  not not_13 (not_13_out, KBD_val[6]);
  Multiplexer #(.select(2), .width(9)) multiplexer_3 (
    .in0(increment_decrement_9bit_1_result), .in1({OPCODE, {5{1'b0}}}), .in2({9{1'b0}}),
    .in3(multiplexer_1_out), .out(multiplexer_3_out), .sel(MUX_in));
  Comparator #(.mode("unsigned"), .width(4)) comparator_1 (
    .a(KBD_val[3:0]), .b(4'b0000), .gt(comparator_1_gt), .eq(comparator_1_eq));  // open: lt
  Comparator #(.mode("unsigned"), .width(4)) comparator_2 (
    .a(KBD_val[3:0]), .b(4'b1010), .lt(comparator_2_lt));  // open: gt, eq
  Register_9bit register_9bit_1 (.EN(En), .CLK(CLK), .D(multiplexer_3_out), .Result(Result));
  or or_1 (or_1_out, comparator_1_gt, comparator_1_eq);
  and and_6 (and_6_out, or_1_out, comparator_2_lt);
endmodule

module Register_8bit_with_clear (
  input  EN,
  input  CLK,
  input  [7:0] D,
  input  CLR,
  output [7:0] Result
);

  wire or_1_out;
  wire [7:0] multiplexer_1_out;

  Multiplexer #(.width(8)) multiplexer_1 (.in0(D), .in1({8{1'b0}}), .out(multiplexer_1_out), .sel(CLR));
  or or_1 (or_1_out, EN, CLR);
  Register_1bit register_1bit_1 (.D(multiplexer_1_out[0]), .En(or_1_out), .CLK(CLK), .Q(Result[0]));
  Register_1bit register_1bit_2 (.D(multiplexer_1_out[1]), .En(or_1_out), .CLK(CLK), .Q(Result[1]));
  Register_1bit register_1bit_3 (.D(multiplexer_1_out[2]), .En(or_1_out), .CLK(CLK), .Q(Result[2]));
  Register_1bit register_1bit_4 (.D(multiplexer_1_out[3]), .En(or_1_out), .CLK(CLK), .Q(Result[3]));
  Register_1bit register_1bit_5 (.D(multiplexer_1_out[4]), .En(or_1_out), .CLK(CLK), .Q(Result[4]));
  Register_1bit register_1bit_6 (.D(multiplexer_1_out[5]), .En(or_1_out), .CLK(CLK), .Q(Result[5]));
  Register_1bit register_1bit_7 (.D(multiplexer_1_out[6]), .En(or_1_out), .CLK(CLK), .Q(Result[6]));
  Register_1bit register_1bit_8 (.D(multiplexer_1_out[7]), .En(or_1_out), .CLK(CLK), .Q(Result[7]));
endmodule

module Add_Sub_otherBit (
  input  A,
  input  B,
  input  Mode,
  input  Cin,
  output Cout,
  output Sum
);

  wire and_1_out, and_2_out, xor_1_out, xor_2_out;

  xor xor_1 (xor_1_out, B, Mode);
  and and_1 (and_1_out, A, xor_1_out);
  xor xor_2 (xor_2_out, A, xor_1_out);
  and and_2 (and_2_out, Cin, xor_2_out);
  xor xor_3 (Sum, xor_2_out, Cin);
  or or_1 (Cout, and_1_out, and_2_out);
endmodule

module Stack_Pointer (
  input  RESET,
  input  En,
  input  CLK,
  input  Inc,
  input  [7:0] D,
  input  S0,
  input  S1,
  output [7:0] Result
);

  wire not_1_out, not_2_out, or_1_out;
  wire [1:0] and_1_out;
  wire [7:0] increment_decrement_8bit_1_result, multiplexer_1_out;

  not not_1 (not_1_out, RESET);
  or or_1 (or_1_out, RESET, En);
  not not_2 (not_2_out, Inc);
  Increment_Decrement_8bit increment_decrement_8bit_1 (
    .A(Result), .Mode(not_2_out), .Result(increment_decrement_8bit_1_result));
  and and_1 (and_1_out[0], not_1_out, S0);
  or or_2 (and_1_out[1], RESET, S1);
  Multiplexer #(.select(2), .width(8)) multiplexer_1 (
    .in0(increment_decrement_8bit_1_result), .in1(D), .in2({8{1'b1}}), .out(multiplexer_1_out),
    .sel(and_1_out));  // open: in3
  Register_8bit register_8bit_1 (.EN(or_1_out), .CLK(CLK), .D(multiplexer_1_out), .Result(Result));
endmodule

module Register_9bit (
  input  EN,
  input  CLK,
  input  [8:0] D,
  output [8:0] Result
);

  Register_1bit register_1bit_1 (.D(D[0]), .En(EN), .CLK(CLK), .Q(Result[0]));
  Register_1bit register_1bit_2 (.D(D[1]), .En(EN), .CLK(CLK), .Q(Result[1]));
  Register_1bit register_1bit_3 (.D(D[2]), .En(EN), .CLK(CLK), .Q(Result[2]));
  Register_1bit register_1bit_4 (.D(D[3]), .En(EN), .CLK(CLK), .Q(Result[3]));
  Register_1bit register_1bit_5 (.D(D[4]), .En(EN), .CLK(CLK), .Q(Result[4]));
  Register_1bit register_1bit_6 (.D(D[5]), .En(EN), .CLK(CLK), .Q(Result[5]));
  Register_1bit register_1bit_7 (.D(D[6]), .En(EN), .CLK(CLK), .Q(Result[6]));
  Register_1bit register_1bit_8 (.D(D[7]), .En(EN), .CLK(CLK), .Q(Result[7]));
  Register_1bit register_1bit_9 (.D(D[8]), .En(EN), .CLK(CLK), .Q(Result[8]));
endmodule

module Increment_Decrement_9bit (
  input  [8:0] A,
  input  Mode,
  output [8:0] Result
);

  wire add_sub_firstbit_1_cout, add_sub_otherbit_1_cout, add_sub_otherbit_2_cout, add_sub_otherbit_3_cout,
       add_sub_otherbit_4_cout, add_sub_otherbit_5_cout, add_sub_otherbit_6_cout, add_sub_otherbit_7_cout;

  Add_Sub_firstBit add_sub_firstbit_1 (
    .A(A[0]), .B(1'b1), .Mode(Mode), .Sum(Result[0]), .Cout(add_sub_firstbit_1_cout));
  Add_Sub_otherBit add_sub_otherbit_1 (
    .A(A[1]), .B(1'b0), .Mode(Mode), .Cin(add_sub_firstbit_1_cout), .Sum(Result[1]),
    .Cout(add_sub_otherbit_1_cout));
  Add_Sub_otherBit add_sub_otherbit_2 (
    .A(A[2]), .B(1'b0), .Mode(Mode), .Cin(add_sub_otherbit_1_cout), .Sum(Result[2]),
    .Cout(add_sub_otherbit_2_cout));
  Add_Sub_otherBit add_sub_otherbit_3 (
    .A(A[3]), .B(1'b0), .Mode(Mode), .Cin(add_sub_otherbit_2_cout), .Sum(Result[3]),
    .Cout(add_sub_otherbit_3_cout));
  Add_Sub_otherBit add_sub_otherbit_4 (
    .A(A[4]), .B(1'b0), .Mode(Mode), .Cin(add_sub_otherbit_3_cout), .Sum(Result[4]),
    .Cout(add_sub_otherbit_4_cout));
  Add_Sub_otherBit add_sub_otherbit_5 (
    .A(A[5]), .B(1'b0), .Mode(Mode), .Cin(add_sub_otherbit_4_cout), .Sum(Result[5]),
    .Cout(add_sub_otherbit_5_cout));
  Add_Sub_otherBit add_sub_otherbit_6 (
    .A(A[6]), .B(1'b0), .Mode(Mode), .Cin(add_sub_otherbit_5_cout), .Sum(Result[6]),
    .Cout(add_sub_otherbit_6_cout));
  Add_Sub_otherBit add_sub_otherbit_7 (
    .A(A[7]), .B(Mode), .Mode(1'b0), .Cin(add_sub_otherbit_6_cout), .Sum(Result[7]),
    .Cout(add_sub_otherbit_7_cout));
  Add_Sub_otherBit add_sub_otherbit_8 (
    .A(A[8]), .B(1'b0), .Cin(add_sub_otherbit_7_cout), .Sum(Result[8]));  // open: Mode, Cout
endmodule

module INT_Enable (
  input  RESET,
  input  EN,
  input  CLK,
  input  D,
  output Q
);

  wire controlled_buffer_1_out, not_1_out, or_1_out;

  not not_1 (not_1_out, RESET);
  assign controlled_buffer_1_out = RESET ? 1'b1 : 1'bz;  // Controlled_Buffer controlled_buffer_1
  assign controlled_buffer_1_out = not_1_out ? D : 1'bz;  // Controlled_Buffer controlled_buffer_2
  or or_1 (or_1_out, RESET, EN);
  Register_1bit register_1bit_1 (.D(controlled_buffer_1_out), .En(or_1_out), .CLK(CLK), .Q(Q));
endmodule

module INT_Pending (
  input  CLK,
  input  En,
  input  D,
  input  CLR,
  output Q
);

  wire multiplexer_1_out, or_1_out, or_2_out;

  or or_1 (or_1_out, Q, D);
  Multiplexer multiplexer_1 (.in0(or_1_out), .in1(1'b0), .out(multiplexer_1_out), .sel(CLR));
  or or_2 (or_2_out, CLR, En);
  Register_1bit register_1bit_1 (.D(multiplexer_1_out), .En(or_2_out), .CLK(CLK), .Q(Q));
endmodule
