// Logisim project 8bit_cpu_current.circ as structural Verilog: 24 circuits, main circuit main
module main (
  input  RUN,
  input  SM_IE,
  input  CLK,
  input  D0,
  input  S0,
  input  S1,
  input  D1,
  input  in_8,
  output exit_enable,
  output loop_enable,
  output is_dec,
  output [2:0] substates,
  output is_wb,
  output is_exe,
  output LDA_KBD,
  output [7:0] out_16,
  output digit_valid,
  output LDA_KBD_1,
  output is_enter,
  output [7:0] out_20,
  output [7:0] out_21,
  output [7:0] out_22,
  output [7:0] out_23,
  output [7:0] out_24,
  output [7:0] out_25,
  output [1:0] state
);

  wire and_1_out, and_2_out, and_3_out, and_4_out, and_5_out, and_6_out, and_7_out, and_9_out, and_11_out,
       and_13_out, and_15_out, and_16_out, and_17_out, and_18_out, and_19_out, and_20_out, and_21_out,
       and_22_out, and_23_out, and_24_out, and_25_out, and_26_out, and_29_out, and_30_out, comparator_1_eq,
       comparator_1_gt, comparator_2_lt, comparator_3_eq, comparator_4_eq, controlled_buffer_1_out,
       controlled_buffer_10_out, controlled_inverter_1_out, decode_1_add, decode_1_hlt, decode_1_jc,
       decode_1_jmp, decode_1_jz, decode_1_lda, decode_1_sta, decode_1_sub, not_1_out, not_2_out, not_3_out,
       not_4_out, not_5_out, not_6_out, not_7_out, not_8_out, not_9_out, not_10_out, not_11_out, not_12_out,
       not_13_out, not_14_out, not_15_out, not_16_out, not_17_out, not_18_out, not_19_out, not_20_out,
       not_21_out, not_22_out, not_23_out, not_24_out, not_25_out, not_26_out, not_27_out, not_28_out,
       not_29_out, not_30_out, not_31_out, not_32_out, not_33_out, or_1_out, or_2_out, or_3_out, or_4_out,
       or_5_out, or_6_out, or_7_out, or_8_out, or_9_out, or_10_out, or_11_out, or_12_out, or_13_out,
       or_14_out, or_15_out, the8bitadderwithmodes_1_carry, the8bitadderwithmodes_1_zero;
  wire [3:0] controlled_buffer_6_out, instruction_register_1_ir_out;
  wire [6:0] keyboard_1_data;
  wire [7:0] controlled_buffer_3_out, controlled_buffer_4_out, controlled_buffer_5_out,
       controlled_buffer_7_out, controlled_buffer_8_out, controlled_buffer_11_out, controlled_buffer_15_out,
       controlled_buffer_16_out, controlled_buffer_28_out, controlled_buffer_29_out,
       controlled_buffer_30_out, controlled_buffer_31_out, controlled_buffer_32_out,
       controlled_buffer_33_out, Output_Register_result, program_counter_1_result, Register_A_result,
       rom_1_data, shifter_1_out, shifter_2_out, the8bitadderwithmodes_1_result;
  wire [7:4] instruction_register_1_ir_out_2;

  and and_1 (and_1_out, RUN, and_2_out);
  not not_1 (not_1_out, and_5_out);
  assign controlled_buffer_1_out = not_1_out ? S0 : 1'bz;  // Controlled_Buffer controlled_buffer_1
  assign controlled_buffer_1_out = and_5_out ? and_5_out : 1'bz;  // Controlled_Buffer controlled_buffer_2
  ROM rom_1 (.addr(controlled_buffer_4_out), .data(rom_1_data));
  and and_2 (and_2_out, CLK, not_2_out);
  or or_1 (or_1_out, and_3_out, and_5_out);
  assign controlled_buffer_3_out = and_5_out ? {4'b0000, instruction_register_1_ir_out} : 8'bz;  // Controlled_Buffer controlled_buffer_3
  not not_2 (not_2_out, decode_1_hlt);
  and and_3 (and_3_out, not_3_out, not_4_out);
  and and_4 (and_4_out, not_3_out, state[1]);
  and and_5 (and_5_out, and_4_out, or_2_out);
  not not_3 (not_3_out, state[0]);
  not not_4 (not_4_out, state[1]);
  Program_Counter program_counter_1 (
    .En(or_1_out), .CLK(and_1_out), .Manual_data(controlled_buffer_3_out), .S0(controlled_buffer_1_out),
    .S1(S1), .Result(program_counter_1_result));
  Instruction_Register instruction_register_1 (
    .Load(and_3_out), .CLK(and_1_out), .data_in(controlled_buffer_5_out),
    .ir_out({instruction_register_1_ir_out_2, instruction_register_1_ir_out}));
  State_Machine state_machine_1 (
    .loop_en(loop_enable), .exit_en(exit_enable), .IS_LDA_KBD(LDA_KBD), .CLK(and_1_out), .En(SM_IE),
    .Substate_Increment(1'b1), .State(state), .Substate(substates));
  assign controlled_buffer_4_out = and_3_out ? program_counter_1_result : 8'bz;  // Controlled_Buffer controlled_buffer_4
  assign controlled_buffer_5_out = and_3_out ? rom_1_data : 8'bz;  // Controlled_Buffer controlled_buffer_5
  and and_6 (and_6_out, or_4_out, not_12_out, decode_1_sta);
  and and_7 (and_7_out, instruction_register_1_ir_out[0], instruction_register_1_ir_out[1], instruction_register_1_ir_out[2], instruction_register_1_ir_out[3], not_5_out, instruction_register_1_ir_out_2[5], not_6_out, not_7_out);
  not not_5 (not_5_out, instruction_register_1_ir_out_2[4]);
  not not_6 (not_6_out, instruction_register_1_ir_out_2[6]);
  not not_7 (not_7_out, instruction_register_1_ir_out_2[7]);
  not not_8 (not_8_out, instruction_register_1_ir_out[0]);
  and and_8 (LDA_KBD, not_8_out, instruction_register_1_ir_out[1], instruction_register_1_ir_out[2], instruction_register_1_ir_out[3], instruction_register_1_ir_out_2[4], not_9_out, not_10_out, not_11_out);
  not not_9 (not_9_out, instruction_register_1_ir_out_2[5]);
  not not_10 (not_10_out, instruction_register_1_ir_out_2[6]);
  not not_11 (not_11_out, instruction_register_1_ir_out_2[7]);
  or or_2 (or_2_out, and_16_out, and_15_out, decode_1_jmp);
  not not_12 (not_12_out, and_7_out);
  RAM #(.addrWidth(4)) ram_1 (
    .addr(controlled_buffer_6_out), .we(and_6_out), .oe(and_11_out), .clk(and_2_out),
    .din(controlled_buffer_7_out), .dout(out_22));
  assign controlled_buffer_6_out = or_3_out ? instruction_register_1_ir_out : 4'bz;  // Controlled_Buffer controlled_buffer_6
  assign controlled_buffer_7_out = and_6_out ? Register_A_result : 8'bz;  // Controlled_Buffer controlled_buffer_7
  Decode decode_1 (
    .Opcode(instruction_register_1_ir_out_2), .LDA(decode_1_lda), .ADD(decode_1_add), .HLT(decode_1_hlt),
    .STA(decode_1_sta), .SUB(decode_1_sub), .JMP(decode_1_jmp), .JZ(decode_1_jz), .JC(decode_1_jc));
  or or_3 (or_3_out, decode_1_sub, decode_1_sta, decode_1_add, decode_1_lda);
  and and_9 (and_9_out, or_4_out, and_7_out);
  not not_13 (not_13_out, state[0]);
  and and_10 (is_exe, state[1], not_13_out);
  or or_4 (or_4_out, is_exe, is_wb);
  and and_11 (and_11_out, or_3_out, or_4_out);
  and and_12 (is_wb, state[1], state[0]);
  not not_14 (not_14_out, state[1]);
  not not_15 (not_15_out, LDA_KBD);
  and and_13 (and_13_out, is_wb, not_15_out, decode_1_lda);
  assign controlled_buffer_8_out = and_13_out ? out_22 : 8'bz;  // Controlled_Buffer controlled_buffer_8
  assign controlled_buffer_8_out = and_17_out ? the8bitadderwithmodes_1_result : 8'bz;  // Controlled_Buffer controlled_buffer_9
  and and_14 (is_dec, state[0], not_14_out);
  and and_15 (and_15_out, decode_1_jc, the8bitadderwithmodes_1_carry);
  Register_8bit Output_Register (
    .EN(and_9_out), .CLK(and_2_out), .D(Register_A_result), .Result(Output_Register_result));
  LedBar LED_output (
    .led0(Output_Register_result[7]), .led1(Output_Register_result[6]), .led2(Output_Register_result[5]),
    .led3(Output_Register_result[4]), .led4(Output_Register_result[3]), .led5(Output_Register_result[2]),
    .led6(Output_Register_result[1]), .led7(Output_Register_result[0]));
  and and_16 (and_16_out, decode_1_jz, the8bitadderwithmodes_1_zero);
  assign controlled_buffer_10_out = decode_1_sub ? decode_1_sub : 1'bz;  // Controlled_Buffer controlled_buffer_10
  assign controlled_inverter_1_out = decode_1_sub ? ~decode_1_sub : 1'bz;  // Controlled_Inverter controlled_inverter_1
  or or_5 (or_5_out, decode_1_sub, decode_1_add);
  and and_17 (and_17_out, is_wb, or_5_out);
  Register_8bit Register_A (.EN(and_11_out), .CLK(and_2_out), .D(controlled_buffer_8_out), .Result(Register_A_result));
  assign controlled_buffer_11_out = and_17_out ? out_22 : 8'bz;  // Controlled_Buffer controlled_buffer_11
  assign controlled_buffer_8_out = and_18_out ? out_25 : 8'bz;  // Controlled_Buffer controlled_buffer_12
  and and_18 (and_18_out, LDA_KBD, state[0], state[1]);
  or or_6 (or_6_out, decode_1_sub, or_7_out, decode_1_add);
  assign controlled_buffer_10_out = decode_1_add ? ~decode_1_add : 1'bz;  // Controlled_Inverter controlled_inverter_2
  assign controlled_buffer_10_out = not_18_out ? D0 : 1'bz;  // Controlled_Buffer controlled_buffer_13
  assign controlled_inverter_1_out = decode_1_add ? ~decode_1_add : 1'bz;  // Controlled_Inverter controlled_inverter_3
  assign controlled_inverter_1_out = not_18_out ? D1 : 1'bz;  // Controlled_Buffer controlled_buffer_14
  assign controlled_buffer_15_out = not_16_out ? Register_A_result : 8'bz;  // Controlled_Buffer controlled_buffer_15
  assign controlled_buffer_16_out = not_16_out ? controlled_buffer_11_out : 8'bz;  // Controlled_Buffer controlled_buffer_16
  assign controlled_buffer_11_out = not_17_out ? {8{1'b0}} : 8'bz;  // Controlled_Buffer controlled_buffer_17
  not not_16 (not_16_out, LDA_KBD);
  not not_17 (not_17_out, and_17_out);
  and and_19 (and_19_out, is_exe, LDA_KBD);
  and and_20 (and_20_out, LDA_KBD, is_dec);
  not not_18 (not_18_out, or_6_out);
  assign controlled_buffer_10_out = or_8_out ? 1'b0 : 1'bz;  // Controlled_Buffer controlled_buffer_18
  assign controlled_inverter_1_out = or_8_out ? 1'b0 : 1'bz;  // Controlled_Buffer controlled_buffer_19
  assign controlled_buffer_16_out = and_22_out ? 8'h30 : 8'bz;  // Controlled_Buffer controlled_buffer_20
  assign controlled_buffer_15_out = and_25_out ? out_21 : 8'bz;  // Controlled_Buffer controlled_buffer_21
  assign controlled_buffer_15_out = and_26_out ? out_24 : 8'bz;  // Controlled_Buffer controlled_buffer_22
  assign controlled_buffer_16_out = and_26_out ? out_20 : 8'bz;  // Controlled_Buffer controlled_buffer_23
  assign controlled_buffer_16_out = and_25_out ? out_23 : 8'bz;  // Controlled_Buffer controlled_buffer_24
  not not_19 (not_19_out, substates[0]);
  not not_20 (not_20_out, substates[1]);
  not not_21 (not_21_out, substates[2]);
  not not_22 (not_22_out, substates[1]);
  not not_23 (not_23_out, substates[0]);
  not not_24 (not_24_out, substates[2]);
  not not_25 (not_25_out, substates[1]);
  and and_21 (and_21_out, not_21_out, not_22_out, not_23_out, and_19_out);
  and and_22 (and_22_out, not_24_out, not_25_out, digit_valid, substates[0], and_19_out);
  or or_7 (or_7_out, and_22_out, or_8_out);
  Keyboard #(.buflen(8)) keyboard_1 (.clk(CLK), .re(and_21_out), .clr(in_8), .data(keyboard_1_data));  // open: avail
  assign controlled_buffer_15_out = and_22_out ? out_16 : 8'bz;  // Controlled_Buffer controlled_buffer_25
  assign controlled_buffer_10_out = and_22_out ? 1'b1 : 1'bz;  // Controlled_Buffer controlled_buffer_26
  assign controlled_inverter_1_out = and_22_out ? 1'b0 : 1'bz;  // Controlled_Buffer controlled_buffer_27
  and and_23 (and_23_out, not_19_out, not_20_out, substates[2]);
  not not_26 (not_26_out, substates[2]);
  not not_27 (not_27_out, substates[0]);
  not not_28 (not_28_out, substates[2]);
  and and_24 (and_24_out, not_26_out, substates[1], digit_valid, not_27_out, and_19_out);
  or or_8 (or_8_out, and_25_out, and_26_out);
  not not_29 (not_29_out, substates[1]);
  not not_30 (not_30_out, substates[0]);
  and and_25 (and_25_out, not_28_out, substates[1], digit_valid, substates[0], and_19_out);
  and and_26 (and_26_out, substates[2], not_29_out, digit_valid, not_30_out, and_19_out);
  and and_27 (loop_enable, and_23_out, and_19_out, not_31_out);
  not not_31 (not_31_out, is_enter);
  The8BitAdderWithModes the8bitadderwithmodes_1 (
    .A(controlled_buffer_15_out), .B(controlled_buffer_16_out), .EN(and_17_out), .CLK(and_2_out),
    .S0(controlled_buffer_10_out), .S1(controlled_inverter_1_out), .Carry(the8bitadderwithmodes_1_carry),
    .Zero(the8bitadderwithmodes_1_zero), .Result(the8bitadderwithmodes_1_result));
  assign controlled_buffer_28_out = and_21_out ? {1'b0, keyboard_1_data} : 8'bz;  // Controlled_Buffer controlled_buffer_28
  assign controlled_buffer_29_out = and_22_out ? the8bitadderwithmodes_1_result : 8'bz;  // Controlled_Buffer controlled_buffer_29
  assign controlled_buffer_30_out = and_24_out ? shifter_1_out : 8'bz;  // Controlled_Buffer controlled_buffer_30
  Shifter shifter_1 (.in(out_25), .\dist (3'b001), .out(shifter_1_out));
  assign controlled_buffer_31_out = and_24_out ? shifter_2_out : 8'bz;  // Controlled_Buffer controlled_buffer_31
  Shifter shifter_2 (.in(out_25), .\dist (3'b011), .out(shifter_2_out));
  assign controlled_buffer_32_out = and_25_out ? the8bitadderwithmodes_1_result : 8'bz;  // Controlled_Buffer controlled_buffer_32
  assign controlled_buffer_33_out = and_26_out ? the8bitadderwithmodes_1_result : 8'bz;  // Controlled_Buffer controlled_buffer_33
  and and_28 (exit_enable, and_19_out, is_enter);
  or or_9 (or_9_out, and_20_out, and_21_out);
  assign controlled_buffer_28_out = and_20_out ? {8{1'b0}} : 8'bz;  // Controlled_Buffer controlled_buffer_34
  or or_10 (or_10_out, and_20_out, and_22_out);
  assign controlled_buffer_29_out = and_20_out ? {8{1'b0}} : 8'bz;  // Controlled_Buffer controlled_buffer_35
  or or_11 (or_11_out, and_24_out, and_20_out);
  assign controlled_buffer_30_out = and_20_out ? {8{1'b0}} : 8'bz;  // Controlled_Buffer controlled_buffer_36
  or or_12 (or_12_out, and_24_out, and_20_out);
  assign controlled_buffer_31_out = and_20_out ? {8{1'b0}} : 8'bz;  // Controlled_Buffer controlled_buffer_37
  or or_13 (or_13_out, and_25_out, and_20_out);
  assign controlled_buffer_32_out = and_20_out ? {8{1'b0}} : 8'bz;  // Controlled_Buffer controlled_buffer_38
  or or_14 (or_14_out, and_26_out, and_20_out);
  assign controlled_buffer_33_out = and_20_out ? {8{1'b0}} : 8'bz;  // Controlled_Buffer controlled_buffer_39
  Register_8bit TEMP (.EN(or_9_out), .CLK(CLK), .D(controlled_buffer_28_out), .Result(out_16));
  Register_8bit DIGIT (.EN(or_10_out), .CLK(CLK), .D(controlled_buffer_29_out), .Result(out_20));
  Register_8bit TEMP1 (.EN(or_11_out), .CLK(CLK), .D(controlled_buffer_30_out), .Result(out_21));
  Register_8bit TEMP2 (.EN(or_12_out), .CLK(CLK), .D(controlled_buffer_31_out), .Result(out_23));
  Register_8bit TEMP3 (.EN(or_13_out), .CLK(CLK), .D(controlled_buffer_32_out), .Result(out_24));
  Register_8bit ACCUMULATOR (.EN(or_14_out), .CLK(CLK), .D(controlled_buffer_33_out), .Result(out_25));
  not not_32 (not_32_out, out_16[6]);
  not not_33 (not_33_out, out_16[7]);
  Comparator #(.mode("unsigned"), .width(4)) comparator_1 (
    .a(out_16[3:0]), .b(4'b0000), .gt(comparator_1_gt), .eq(comparator_1_eq));  // open: lt
  Comparator #(.mode("unsigned"), .width(4)) comparator_2 (
    .a(out_16[3:0]), .b(4'b1010), .lt(comparator_2_lt));  // open: gt, eq
  and and_29 (and_29_out, out_16[4], out_16[5], not_32_out, not_33_out);
  Comparator #(.mode("unsigned")) comparator_3 (.a(out_16), .b(8'ha), .eq(comparator_3_eq));  // open: gt, lt
  Comparator comparator_4 (.a(out_16), .b({8{1'b0}}), .eq(comparator_4_eq));  // open: gt, lt
  or or_15 (or_15_out, comparator_1_gt, comparator_1_eq);
  and and_30 (and_30_out, or_15_out, comparator_2_lt);
  or or_16 (is_enter, comparator_3_eq, comparator_4_eq);
  and and_31 (digit_valid, and_30_out, and_29_out);

  assign LDA_KBD_1 = LDA_KBD;

  // Notes on the sheet:
  //   contents of rom_1 (hex, n*v repeats v):
  //   1e 1e 20 42 56 e0 f0
endmodule

module FirstBit (
  input  A,
  input  B,
  input  Mode,
  output OR_Out,
  output AND_Out,
  output Cout,
  output Sum
);

  wire and_2_out, and_3_out, xor_1_out, xor_2_out;

  xor xor_1 (xor_1_out, B, Mode);
  or or_1 (OR_Out, A, B);
  and and_1 (AND_Out, A, B);
  and and_2 (and_2_out, A, xor_1_out);
  xor xor_2 (xor_2_out, A, xor_1_out);
  and and_3 (and_3_out, Mode, xor_2_out);
  xor xor_3 (Sum, xor_2_out, Mode);
  or or_2 (Cout, and_2_out, and_3_out);
endmodule

module OtherBit (
  input  A,
  input  B,
  input  Mode,
  input  Cin,
  output OR_Out,
  output AND_Out,
  output Cout,
  output Sum
);

  wire and_2_out, and_3_out, xor_1_out, xor_2_out;

  xor xor_1 (xor_1_out, B, Mode);
  or or_1 (OR_Out, A, B);
  and and_1 (AND_Out, A, B);
  and and_2 (and_2_out, A, xor_1_out);
  xor xor_2 (xor_2_out, A, xor_1_out);
  or or_2 (Cout, and_2_out, and_3_out);
  and and_3 (and_3_out, Cin, xor_2_out);
  xor xor_3 (Sum, xor_2_out, Cin);
endmodule

module The8BitAdderWithModes (
  input  [7:0] A,
  input  [7:0] B,
  input  EN,
  input  CLK,
  input  S0,
  input  S1,
  output Carry,
  output Zero,
  output [7:0] Result
);

  wire firstbit_1_cout, otherbit_1_cout, otherbit_2_cout, otherbit_3_cout, otherbit_4_cout, otherbit_5_cout,
       otherbit_6_cout, otherbit_7_cout;
  wire [7:0] firstbit_1_and_out, firstbit_1_or_out, firstbit_1_sum;

  FirstBit firstbit_1 (
    .A(A[0]), .B(B[0]), .Mode(S0), .OR_Out(firstbit_1_or_out[0]), .AND_Out(firstbit_1_and_out[0]),
    .Sum(firstbit_1_sum[0]), .Cout(firstbit_1_cout));
  OtherBit otherbit_1 (
    .A(A[1]), .B(B[1]), .Mode(S0), .Cin(firstbit_1_cout), .AND_Out(firstbit_1_and_out[1]),
    .OR_Out(firstbit_1_or_out[1]), .Sum(firstbit_1_sum[1]), .Cout(otherbit_1_cout));
  OtherBit otherbit_2 (
    .A(A[2]), .B(B[2]), .Mode(S0), .Cin(otherbit_1_cout), .AND_Out(firstbit_1_and_out[2]),
    .OR_Out(firstbit_1_or_out[2]), .Sum(firstbit_1_sum[2]), .Cout(otherbit_2_cout));
  OtherBit otherbit_3 (
    .A(A[3]), .B(B[3]), .Mode(S0), .Cin(otherbit_2_cout), .AND_Out(firstbit_1_and_out[3]),
    .OR_Out(firstbit_1_or_out[3]), .Sum(firstbit_1_sum[3]), .Cout(otherbit_3_cout));
  OtherBit otherbit_4 (
    .A(A[4]), .B(B[4]), .Mode(S0), .Cin(otherbit_3_cout), .AND_Out(firstbit_1_and_out[4]),
    .OR_Out(firstbit_1_or_out[4]), .Sum(firstbit_1_sum[4]), .Cout(otherbit_4_cout));
  OtherBit otherbit_5 (
    .A(A[5]), .B(B[5]), .Mode(S0), .Cin(otherbit_4_cout), .AND_Out(firstbit_1_and_out[5]),
    .OR_Out(firstbit_1_or_out[5]), .Sum(firstbit_1_sum[5]), .Cout(otherbit_5_cout));
  OtherBit otherbit_6 (
    .A(A[6]), .B(B[6]), .Mode(S0), .Cin(otherbit_5_cout), .AND_Out(firstbit_1_and_out[6]),
    .OR_Out(firstbit_1_or_out[6]), .Sum(firstbit_1_sum[6]), .Cout(otherbit_6_cout));
  OtherBit otherbit_7 (
    .A(A[7]), .B(B[7]), .Mode(S0), .Cin(otherbit_6_cout), .AND_Out(firstbit_1_and_out[7]),
    .OR_Out(firstbit_1_or_out[7]), .Sum(firstbit_1_sum[7]), .Cout(otherbit_7_cout));
  Multiplexer #(.select(2), .width(8)) multiplexer_1 (
    .in0(firstbit_1_sum), .in1(firstbit_1_sum), .in2(firstbit_1_or_out), .in3(firstbit_1_and_out),
    .out(Result), .sel({S1, S0}));
  nor nor_1 (Zero, Result[0], Result[1], Result[2], Result[3], Result[4], Result[5], Result[6], Result[7]);
  Register_1bit register_1bit_1 (.D(otherbit_7_cout), .En(EN), .CLK(CLK), .Q(Carry));
endmodule

module Register_1bit (
  input  D,
  input  En,
  input  CLK,
  output Q
);

  wire and_1_out, and_2_out, not_1_out, or_1_out;

  not not_1 (not_1_out, En);
  and and_1 (and_1_out, D, En);
  and and_2 (and_2_out, not_1_out, Q);
  or or_1 (or_1_out, and_1_out, and_2_out);
  D_Flip_Flop d_ff_1 (.D(or_1_out), .clk(CLK), .Q(Q));  // open: Qn, preset, reset
endmodule

module Register_8bit (
  input  EN,
  input  CLK,
  input  [7:0] D,
  output [7:0] Result
);

  Register_1bit register_1bit_1 (.D(D[0]), .En(EN), .CLK(CLK), .Q(Result[0]));
  Register_1bit register_1bit_2 (.D(D[1]), .En(EN), .CLK(CLK), .Q(Result[1]));
  Register_1bit register_1bit_3 (.D(D[2]), .En(EN), .CLK(CLK), .Q(Result[2]));
  Register_1bit register_1bit_4 (.D(D[3]), .En(EN), .CLK(CLK), .Q(Result[3]));
  Register_1bit register_1bit_5 (.D(D[4]), .En(EN), .CLK(CLK), .Q(Result[4]));
  Register_1bit register_1bit_6 (.D(D[5]), .En(EN), .CLK(CLK), .Q(Result[5]));
  Register_1bit register_1bit_7 (.D(D[6]), .En(EN), .CLK(CLK), .Q(Result[6]));
  Register_1bit register_1bit_8 (.D(D[7]), .En(EN), .CLK(CLK), .Q(Result[7]));
endmodule

module Register_A_B (
  input  CLK,
  input  A_load,
  input  [7:0] DataA,
  input  B_load,
  input  [7:0] DataB,
  output [7:0] A_out,
  output [7:0] B_out
);

  Register_8bit Register_A (.EN(A_load), .CLK(CLK), .D(DataA), .Result(A_out));
  Register_8bit Register_B (.EN(B_load), .CLK(CLK), .D(DataB), .Result(B_out));
endmodule

module Program_Counter (
  input  En,
  input  CLK,
  input  [7:0] Manual_data,
  input  S0,
  input  S1,
  output [7:0] Result
);

  wire [7:0] adder_8bit_forpc_1_result, multiplexer_1_out;

  Adder_8Bit_forPC adder_8bit_forpc_1 (.A(Result), .Result(adder_8bit_forpc_1_result));
  Multiplexer #(.select(2), .width(8)) multiplexer_1 (
    .in0(adder_8bit_forpc_1_result), .in1(Manual_data), .in2({8{1'b0}}), .out(multiplexer_1_out),
    .sel({S1, S0}));  // open: in3
  Register_8bit register_8bit_1 (.EN(En), .CLK(CLK), .D(multiplexer_1_out), .Result(Result));
endmodule

module Adder_8Bit_forPC (
  input  [7:0] A,
  output [7:0] Result
);

  wire adder_1bit_1_cout, adder_1bit_2_cout, adder_1bit_3_cout, adder_1bit_4_cout, adder_1bit_5_cout,
       adder_1bit_6_cout, adder_1bit_7_cout;

  Adder_1Bit adder_1bit_1 (.A(A[0]), .B(1'b1), .Cin(1'b0), .Sum(Result[0]), .Cout(adder_1bit_1_cout));
  Adder_1Bit adder_1bit_2 (.A(A[1]), .B(1'b0), .Cin(adder_1bit_1_cout), .Sum(Result[1]), .Cout(adder_1bit_2_cout));
  Adder_1Bit adder_1bit_3 (.A(A[2]), .B(1'b0), .Cin(adder_1bit_2_cout), .Sum(Result[2]), .Cout(adder_1bit_3_cout));
  Adder_1Bit adder_1bit_4 (.A(A[3]), .B(1'b0), .Cin(adder_1bit_3_cout), .Sum(Result[3]), .Cout(adder_1bit_4_cout));
  Adder_1Bit adder_1bit_5 (.A(A[4]), .B(1'b0), .Cin(adder_1bit_4_cout), .Sum(Result[4]), .Cout(adder_1bit_5_cout));
  Adder_1Bit adder_1bit_6 (.A(A[5]), .B(1'b0), .Cin(adder_1bit_5_cout), .Sum(Result[5]), .Cout(adder_1bit_6_cout));
  Adder_1Bit adder_1bit_7 (.A(A[6]), .B(1'b0), .Cin(adder_1bit_6_cout), .Sum(Result[6]), .Cout(adder_1bit_7_cout));
  Adder_1Bit adder_1bit_8 (.A(A[7]), .B(1'b0), .Cin(adder_1bit_7_cout), .Sum(Result[7]));  // open: Cout
endmodule

module Adder_1Bit (
  input  A,
  input  B,
  input  Cin,
  output Cout,
  output Sum
);

  wire and_1_out, and_2_out, xor_1_out;

  and and_1 (and_1_out, A, B);
  xor xor_1 (xor_1_out, A, B);
  and and_2 (and_2_out, xor_1_out, Cin);
  xor xor_2 (Sum, xor_1_out, Cin);
  or or_1 (Cout, and_1_out, and_2_out);
endmodule

module Instruction_Register (
  input  Load,
  input  CLK,
  input  [7:0] data_in,
  output [7:0] ir_out
);

  Register_8bit register_8bit_1 (.EN(Load), .CLK(CLK), .D(data_in), .Result(ir_out));
endmodule

module IR_ROM_Test (
  input  EN_PC,
  input  CLK,
  input  EN_IR,
  input  [7:0] Manual_data,
  input  S0,
  input  ROM_Out,
  input  S1,
  output [7:0] Output_Bus,
  output [7:0] IR_Out,
  output [7:0] Data_Out
);

  wire not_1_out;
  wire [7:0] Data_Output_data;

  ROM Data_Output (.addr(Output_Bus), .data(Data_Output_data));
  Program_Counter program_counter_1 (
    .En(EN_PC), .CLK(CLK), .Manual_data(Manual_data), .S0(S0), .S1(S1), .Result(Output_Bus));
  not not_1 (not_1_out, CLK);
  assign Data_Out = ROM_Out ? Data_Output_data : 8'bz;  // Controlled_Buffer controlled_buffer_1
  Instruction_Register instruction_register_1 (.Load(EN_IR), .CLK(not_1_out), .data_in(Data_Out), .ir_out(IR_Out));

  // Notes on the sheet:
  //   contents of Data_Output (hex, n*v repeats v):
  //   32 f bc de fa 1a 16 19 18 15 16 17
endmodule

module RAM_ROM (
  input  [3:0] Address,
  input  Write,
  input  Read,
  input  CLK,
  input  [7:0] Data_in,
  output [7:0] ROM_Data,
  output [7:0] RAM_Data
);

  ROM #(.addrWidth(4)) rom_1 (.addr(Address), .data(ROM_Data));
  RAM #(.addrWidth(4)) ram_1 (.addr(Address), .we(Write), .oe(Read), .clk(CLK), .din(Data_in), .dout(RAM_Data));

  // Notes on the sheet:
  //   contents of rom_1 (hex, n*v repeats v):
  //   0 1 2 3 4 5 6 7 8 9 a b c d e f
endmodule

module Busses (
  input  CLK,
  input  A_OE,
  input  A_in,
  input  B_in,
  input  B_OE,
  input  [7:0] Manual_data,
  input  Toggle,
  input  IR_in,
  input  IR_OE,
  output [7:0] MAIN_BUS
);

  wire [7:0] instruction_register_1_ir_out, multiplexer_1_out, register_a_b_1_a_out, register_a_b_1_b_out;

  Multiplexer #(.width(8)) multiplexer_1 (.in0(Manual_data), .in1(MAIN_BUS), .out(multiplexer_1_out), .sel(Toggle));
  Register_A_B register_a_b_1 (
    .CLK(CLK), .A_load(A_in), .DataA(multiplexer_1_out), .B_load(B_in), .DataB(multiplexer_1_out),
    .A_out(register_a_b_1_a_out), .B_out(register_a_b_1_b_out));
  Instruction_Register instruction_register_1 (
    .Load(IR_in), .CLK(CLK), .data_in(multiplexer_1_out), .ir_out(instruction_register_1_ir_out));
  assign MAIN_BUS[0] = A_OE ? register_a_b_1_a_out[0] : 1'bz;  // Controlled_Buffer controlled_buffer_1
  assign MAIN_BUS[1] = A_OE ? register_a_b_1_a_out[1] : 1'bz;  // Controlled_Buffer controlled_buffer_2
  assign MAIN_BUS[2] = A_OE ? register_a_b_1_a_out[2] : 1'bz;  // Controlled_Buffer controlled_buffer_3
  assign MAIN_BUS[3] = A_OE ? register_a_b_1_a_out[3] : 1'bz;  // Controlled_Buffer controlled_buffer_4
  assign MAIN_BUS[4] = A_OE ? register_a_b_1_a_out[4] : 1'bz;  // Controlled_Buffer controlled_buffer_5
  assign MAIN_BUS[5] = A_OE ? register_a_b_1_a_out[5] : 1'bz;  // Controlled_Buffer controlled_buffer_6
  assign MAIN_BUS[6] = A_OE ? register_a_b_1_a_out[6] : 1'bz;  // Controlled_Buffer controlled_buffer_7
  assign MAIN_BUS[7] = A_OE ? register_a_b_1_a_out[7] : 1'bz;  // Controlled_Buffer controlled_buffer_8
  assign MAIN_BUS[0] = B_OE ? register_a_b_1_b_out[0] : 1'bz;  // Controlled_Buffer controlled_buffer_9
  assign MAIN_BUS[1] = B_OE ? register_a_b_1_b_out[1] : 1'bz;  // Controlled_Buffer controlled_buffer_10
  assign MAIN_BUS[2] = B_OE ? register_a_b_1_b_out[2] : 1'bz;  // Controlled_Buffer controlled_buffer_11
  assign MAIN_BUS[3] = B_OE ? register_a_b_1_b_out[3] : 1'bz;  // Controlled_Buffer controlled_buffer_12
  assign MAIN_BUS[4] = B_OE ? register_a_b_1_b_out[4] : 1'bz;  // Controlled_Buffer controlled_buffer_13
  assign MAIN_BUS[5] = B_OE ? register_a_b_1_b_out[5] : 1'bz;  // Controlled_Buffer controlled_buffer_14
  assign MAIN_BUS[6] = B_OE ? register_a_b_1_b_out[6] : 1'bz;  // Controlled_Buffer controlled_buffer_15
  assign MAIN_BUS[7] = B_OE ? register_a_b_1_b_out[7] : 1'bz;  // Controlled_Buffer controlled_buffer_16
  assign MAIN_BUS[0] = IR_OE ? instruction_register_1_ir_out[0] : 1'bz;  // Controlled_Buffer controlled_buffer_17
  assign MAIN_BUS[1] = IR_OE ? instruction_register_1_ir_out[1] : 1'bz;  // Controlled_Buffer controlled_buffer_18
  assign MAIN_BUS[2] = IR_OE ? instruction_register_1_ir_out[2] : 1'bz;  // Controlled_Buffer controlled_buffer_19
  assign MAIN_BUS[3] = IR_OE ? instruction_register_1_ir_out[3] : 1'bz;  // Controlled_Buffer controlled_buffer_20
  assign MAIN_BUS[4] = IR_OE ? instruction_register_1_ir_out[4] : 1'bz;  // Controlled_Buffer controlled_buffer_21
  assign MAIN_BUS[5] = IR_OE ? instruction_register_1_ir_out[5] : 1'bz;  // Controlled_Buffer controlled_buffer_22
  assign MAIN_BUS[6] = IR_OE ? instruction_register_1_ir_out[6] : 1'bz;  // Controlled_Buffer controlled_buffer_23
  assign MAIN_BUS[7] = IR_OE ? instruction_register_1_ir_out[7] : 1'bz;  // Controlled_Buffer controlled_buffer_24
endmodule

module Busses_ModifiedForMain (
  input  CLK,
  input  A_OE,
  input  A_in,
  input  [7:0] A_IR,
  input  B_in,
  input  A_IR_or_Out,
  input  B_RAM_or_Out,
  input  [7:0] B_RAM,
  input  B_OE,
  output [7:0] MAIN_BUS
);

  wire not_1_out;
  wire [7:0] multiplexer_1_out, multiplexer_2_out, register_a_b_1_a_out, register_a_b_1_b_out;

  Multiplexer #(.width(8)) multiplexer_1 (.in0(A_IR), .in1(MAIN_BUS), .out(multiplexer_1_out), .sel(A_IR_or_Out));
  Multiplexer #(.width(8)) multiplexer_2 (.in0(B_RAM), .in1(MAIN_BUS), .out(multiplexer_2_out), .sel(B_RAM_or_Out));
  not not_1 (not_1_out, CLK);
  Register_A_B register_a_b_1 (
    .CLK(not_1_out), .A_load(A_in), .DataA(multiplexer_1_out), .B_load(B_in), .DataB(multiplexer_2_out),
    .A_out(register_a_b_1_a_out), .B_out(register_a_b_1_b_out));
  assign MAIN_BUS[0] = A_OE ? register_a_b_1_a_out[0] : 1'bz;  // Controlled_Buffer controlled_buffer_1
  assign MAIN_BUS[1] = A_OE ? register_a_b_1_a_out[1] : 1'bz;  // Controlled_Buffer controlled_buffer_2
  assign MAIN_BUS[2] = A_OE ? register_a_b_1_a_out[2] : 1'bz;  // Controlled_Buffer controlled_buffer_3
  assign MAIN_BUS[3] = A_OE ? register_a_b_1_a_out[3] : 1'bz;  // Controlled_Buffer controlled_buffer_4
  assign MAIN_BUS[4] = A_OE ? register_a_b_1_a_out[4] : 1'bz;  // Controlled_Buffer controlled_buffer_5
  assign MAIN_BUS[5] = A_OE ? register_a_b_1_a_out[5] : 1'bz;  // Controlled_Buffer controlled_buffer_6
  assign MAIN_BUS[6] = A_OE ? register_a_b_1_a_out[6] : 1'bz;  // Controlled_Buffer controlled_buffer_7
  assign MAIN_BUS[7] = A_OE ? register_a_b_1_a_out[7] : 1'bz;  // Controlled_Buffer controlled_buffer_8
  assign MAIN_BUS[0] = B_OE ? register_a_b_1_b_out[0] : 1'bz;  // Controlled_Buffer controlled_buffer_9
  assign MAIN_BUS[1] = B_OE ? register_a_b_1_b_out[1] : 1'bz;  // Controlled_Buffer controlled_buffer_10
  assign MAIN_BUS[2] = B_OE ? register_a_b_1_b_out[2] : 1'bz;  // Controlled_Buffer controlled_buffer_11
  assign MAIN_BUS[3] = B_OE ? register_a_b_1_b_out[3] : 1'bz;  // Controlled_Buffer controlled_buffer_12
  assign MAIN_BUS[4] = B_OE ? register_a_b_1_b_out[4] : 1'bz;  // Controlled_Buffer controlled_buffer_13
  assign MAIN_BUS[5] = B_OE ? register_a_b_1_b_out[5] : 1'bz;  // Controlled_Buffer controlled_buffer_14
  assign MAIN_BUS[6] = B_OE ? register_a_b_1_b_out[6] : 1'bz;  // Controlled_Buffer controlled_buffer_15
  assign MAIN_BUS[7] = B_OE ? register_a_b_1_b_out[7] : 1'bz;  // Controlled_Buffer controlled_buffer_16
endmodule

module Week_2_Test (
  input  CLK,
  input  IR_in,
  input  PC_in,
  input  [7:0] PC_manual_data,
  input  S0,
  input  ROM_out,
  input  S1,
  input  A_OE,
  input  A_in,
  input  [3:0] Address,
  input  B_in,
  input  Write,
  input  A_IR_or_Out,
  input  Read,
  input  B_RAM_or_Out,
  input  [7:0] RAM_data,
  input  B_OE,
  output [7:0] out_18,
  output [7:0] MAIN_BUS,
  output [7:0] out_20
);

  wire not_1_out;
  wire [7:0] controlled_buffer_1_out, program_counter_1_result, rom_1_data;

  ROM rom_1 (.addr(program_counter_1_result), .data(rom_1_data));
  Program_Counter program_counter_1 (
    .En(PC_in), .CLK(CLK), .Manual_data(PC_manual_data), .S0(S0), .S1(S1), .Result(program_counter_1_result));
  RAM #(.addrWidth(4)) ram_1 (.addr(Address), .we(Write), .oe(Read), .clk(CLK), .din(RAM_data), .dout(out_20));
  not not_1 (not_1_out, CLK);
  assign controlled_buffer_1_out = ROM_out ? rom_1_data : 8'bz;  // Controlled_Buffer controlled_buffer_1
  Instruction_Register instruction_register_1 (
    .Load(IR_in), .CLK(not_1_out), .data_in(controlled_buffer_1_out), .ir_out(out_18));
  Busses_ModifiedForMain busses_modifiedformain_1 (
    .CLK(CLK), .A_OE(A_OE), .A_in(A_in), .A_IR(out_18), .B_in(B_in), .A_IR_or_Out(A_IR_or_Out),
    .B_RAM_or_Out(B_RAM_or_Out), .B_RAM(out_20), .B_OE(B_OE), .MAIN_BUS(MAIN_BUS));

  // Notes on the sheet:
  //   contents of rom_1 (hex, n*v repeats v):
  //   23 45 67 89 ab cd ef
endmodule

module Register_2bit (
  input  CLK,
  input  En,
  input  [1:0] D,
  output [1:0] State
);

  Register_1bit register_1bit_1 (.D(D[0]), .En(En), .CLK(CLK), .Q(State[0]));
  Register_1bit register_1bit_2 (.D(D[1]), .En(En), .CLK(CLK), .Q(State[1]));
endmodule

module Decode (
  input  [3:0] Opcode,
  output LDA,
  output ADD,
  output HLT,
  output STA,
  output SUB,
  output JMP,
  output JZ,
  output JC
);

  wire not_1_out, not_2_out, not_3_out, not_4_out, not_5_out, not_6_out, not_7_out, not_8_out, not_9_out,
       not_10_out, not_11_out, not_12_out, not_13_out, not_14_out, not_15_out, not_16_out;

  not not_1 (not_1_out, Opcode[1]);
  not not_2 (not_2_out, Opcode[2]);
  not not_3 (not_3_out, Opcode[3]);
  not not_4 (not_4_out, Opcode[2]);
  not not_5 (not_5_out, Opcode[3]);
  not not_6 (not_6_out, Opcode[0]);
  not not_7 (not_7_out, Opcode[2]);
  not not_8 (not_8_out, Opcode[3]);
  not not_9 (not_9_out, Opcode[0]);
  not not_10 (not_10_out, Opcode[1]);
  not not_11 (not_11_out, Opcode[3]);
  not not_12 (not_12_out, Opcode[0]);
  not not_13 (not_13_out, Opcode[1]);
  not not_14 (not_14_out, Opcode[3]);
  not not_15 (not_15_out, Opcode[0]);
  not not_16 (not_16_out, Opcode[3]);
  and and_1 (LDA, Opcode[0], not_1_out, not_2_out, not_3_out);
  and and_2 (ADD, Opcode[0], Opcode[1], not_4_out, not_5_out);
  and and_3 (HLT, Opcode[0], Opcode[1], Opcode[2], Opcode[3]);
  and and_4 (STA, not_6_out, Opcode[1], not_7_out, not_8_out);
  and and_5 (SUB, not_9_out, not_10_out, Opcode[2], not_11_out);
  and and_6 (JMP, not_12_out, Opcode[1], Opcode[2], Opcode[3]);
  and and_7 (JZ, Opcode[0], not_13_out, Opcode[2], not_14_out);
  and and_8 (JC, not_15_out, Opcode[1], Opcode[2], not_16_out);
endmodule

module State_Machine (
  input  loop_en,
  input  exit_en,
  input  IS_LDA_KBD,
  input  CLK,
  input  En,
  input  Substate_Increment,
  output [1:0] State,
  output [2:0] Substate
);

  wire and_2_out, and_3_out, not_1_out, not_2_out, not_3_out, or_1_out;
  wire [1:0] rom_1_data;
  wire [2:0] multiplexer_1_out, simple_3bit_adder_sm_1_result;
  wire [3:0] and_1_out;

  ROM #(.addrWidth(6), .dataWidth(2)) rom_1 (.addr({State, and_1_out}), .data(rom_1_data));
  Register_2bit register_2bit_1 (.CLK(CLK), .En(En), .D(rom_1_data), .State(State));
  Register_3Bit register_3bit_1 (.CLK(CLK), .En(Substate_Increment), .D(multiplexer_1_out), .State(and_1_out[2:0]));
  not not_1 (not_1_out, exit_en);
  and and_1 (and_1_out[3], IS_LDA_KBD, not_1_out);
  assign Substate = IS_LDA_KBD ? and_1_out[2:0] : 3'bz;  // Controlled_Buffer controlled_buffer_1
  or or_1 (or_1_out, exit_en, loop_en);
  not not_2 (not_2_out, State[0]);
  and and_2 (and_2_out, State[1], not_2_out);
  not not_3 (not_3_out, or_1_out);
  and and_3 (and_3_out, and_2_out, not_3_out, IS_LDA_KBD);
  Multiplexer #(.width(3)) multiplexer_1 (
    .in0(3'b000), .in1(simple_3bit_adder_sm_1_result), .out(multiplexer_1_out), .sel(and_3_out));
  Simple_3bit_adder_SM simple_3bit_adder_sm_1 (.A(and_1_out[2:0]), .B(3'b001), .Result(simple_3bit_adder_sm_1_result));

  // Notes on the sheet:
  //   contents of rom_1 (hex, n*v repeats v):
  //   9*1 10*2 5*3 2 2 2 13*3 6*2 3 3
endmodule

module Adder_8Bit_ADD (
  input  [7:0] A,
  input  [7:0] B,
  output [7:0] Result
);

  wire adder_1bit_1_cout, adder_1bit_2_cout, adder_1bit_3_cout, adder_1bit_4_cout, adder_1bit_5_cout,
       adder_1bit_6_cout, adder_1bit_7_cout;

  Adder_1Bit adder_1bit_1 (.A(A[0]), .B(B[0]), .Cin(1'b0), .Sum(Result[0]), .Cout(adder_1bit_1_cout));
  Adder_1Bit adder_1bit_2 (.A(A[1]), .B(B[1]), .Cin(adder_1bit_1_cout), .Sum(Result[1]), .Cout(adder_1bit_2_cout));
  Adder_1Bit adder_1bit_3 (.A(A[2]), .B(B[2]), .Cin(adder_1bit_2_cout), .Sum(Result[2]), .Cout(adder_1bit_3_cout));
  Adder_1Bit adder_1bit_4 (.A(A[3]), .B(B[3]), .Cin(adder_1bit_3_cout), .Sum(Result[3]), .Cout(adder_1bit_4_cout));
  Adder_1Bit adder_1bit_5 (.A(A[4]), .B(B[4]), .Cin(adder_1bit_4_cout), .Sum(Result[4]), .Cout(adder_1bit_5_cout));
  Adder_1Bit adder_1bit_6 (.A(A[5]), .B(B[5]), .Cin(adder_1bit_5_cout), .Sum(Result[5]), .Cout(adder_1bit_6_cout));
  Adder_1Bit adder_1bit_7 (.A(A[6]), .B(B[6]), .Cin(adder_1bit_6_cout), .Sum(Result[6]), .Cout(adder_1bit_7_cout));
  Adder_1Bit adder_1bit_8 (.A(A[7]), .B(B[7]), .Cin(adder_1bit_7_cout), .Sum(Result[7]));  // open: Cout
endmodule

module main_old (
  input  CLK,
  input  RUN,
  input  SM_IE,
  input  Default0,
  input  Default1,
  input  S0,
  input  S1,
  input  in_8,
  input  [7:0] Manual_in,
  input  [3:0] Manual_Address,
  output [7:0] out_11,
  output [7:0] out_12,
  output [7:0] out_13,
  output [7:0] out_14,
  output [7:0] out_15,
  output [7:0] out_16
);

  wire ALU_carry, ALU_zero, and_1_out, and_2_out, and_3_out, and_4_out, and_5_out, and_6_out, and_7_out,
       and_8_out, and_9_out, and_10_out, and_11_out, and_12_out, and_13_out, controlled_buffer_2_out,
       controlled_inverter_1_out, controlled_inverter_2_out, decode_1_add, decode_1_hlt, decode_1_jc,
       decode_1_jmp, decode_1_jz, decode_1_lda, decode_1_sta, decode_1_sub, not_1_out, not_2_out, not_3_out,
       not_4_out, not_5_out, not_6_out, not_7_out, not_8_out, not_9_out, or_1_out, or_2_out, or_3_out,
       or_4_out, or_5_out, or_6_out, or_7_out;
  wire [1:0] state_machine_1_state;
  wire [3:0] controlled_buffer_4_out, controlled_buffer_7_out;
  wire [7:0] controlled_buffer_1_out, controlled_buffer_5_out, controlled_buffer_10_out,
       controlled_buffer_13_out, instruction_register_1_ir_out, rom_1_data;

  or or_1 (or_1_out, and_5_out, and_3_out);
  assign controlled_buffer_1_out = and_3_out ? {4'b0000, instruction_register_1_ir_out[3:0]} : 8'bz;  // Controlled_Buffer controlled_buffer_1
  assign controlled_buffer_2_out = and_3_out ? and_3_out : 1'bz;  // Controlled_Buffer controlled_buffer_2
  not not_1 (not_1_out, and_3_out);
  assign controlled_buffer_2_out = not_1_out ? S0 : 1'bz;  // Controlled_Buffer controlled_buffer_3
  not not_2 (not_2_out, decode_1_hlt);
  and and_1 (and_1_out, CLK, not_2_out);
  and and_2 (and_2_out, RUN, and_1_out);
  and and_3 (and_3_out, and_4_out, or_2_out);
  and and_4 (and_4_out, not_3_out, state_machine_1_state[1]);
  Program_Counter program_counter_1 (
    .En(or_1_out), .CLK(and_2_out), .Manual_data(controlled_buffer_1_out), .S0(controlled_buffer_2_out),
    .S1(S1), .Result(out_11));
  not not_3 (not_3_out, state_machine_1_state[0]);
  and and_5 (and_5_out, not_3_out, not_4_out);
  not not_4 (not_4_out, state_machine_1_state[1]);
  ROM #(.addrWidth(4)) rom_1 (.addr(controlled_buffer_4_out), .data(rom_1_data));
  assign controlled_buffer_4_out = and_5_out ? out_11[3:0] : 4'bz;  // Controlled_Buffer controlled_buffer_4
  State_Machine state_machine_1 (
    .loop_en(and_2_out), .IS_LDA_KBD(SM_IE), .En(and_5_out), .State(state_machine_1_state));  // open: exit_en, CLK, Substate_Increment, Substate
  assign controlled_buffer_5_out = and_5_out ? rom_1_data : 8'bz;  // Controlled_Buffer controlled_buffer_5
  Instruction_Register instruction_register_1 (
    .Load(and_5_out), .CLK(and_2_out), .data_in(controlled_buffer_5_out),
    .ir_out(instruction_register_1_ir_out));
  or or_2 (or_2_out, and_11_out, and_12_out, decode_1_jmp);
  not not_5 (not_5_out, and_6_out);
  assign out_13 = not_5_out ? Manual_in : 8'bz;  // Controlled_Buffer controlled_buffer_6
  Decode decode_1 (
    .Opcode(instruction_register_1_ir_out[7:4]), .LDA(decode_1_lda), .ADD(decode_1_add), .HLT(decode_1_hlt),
    .STA(decode_1_sta), .SUB(decode_1_sub), .JMP(decode_1_jmp), .JZ(decode_1_jz), .JC(decode_1_jc));
  or or_3 (or_3_out, decode_1_sub, decode_1_sta, decode_1_add, decode_1_lda);
  assign controlled_buffer_7_out = or_3_out ? instruction_register_1_ir_out[3:0] : 4'bz;  // Controlled_Buffer controlled_buffer_7
  and and_6 (and_6_out, or_5_out, decode_1_sta);
  or or_4 (or_4_out, in_8, and_6_out);
  assign controlled_buffer_7_out = not_6_out ? Manual_Address : 4'bz;  // Controlled_Buffer controlled_buffer_8
  not not_6 (not_6_out, or_3_out);
  RAM #(.addrWidth(4)) ram_1 (
    .addr(controlled_buffer_7_out), .we(or_4_out), .oe(and_9_out), .clk(and_1_out), .din(out_13),
    .dout(out_14));
  assign out_13 = and_6_out ? out_12 : 8'bz;  // Controlled_Buffer controlled_buffer_9
  not not_7 (not_7_out, state_machine_1_state[0]);
  and and_7 (and_7_out, state_machine_1_state[1], not_7_out);
  or or_5 (or_5_out, and_7_out, and_8_out);
  and and_8 (and_8_out, state_machine_1_state[1], state_machine_1_state[0]);
  and and_9 (and_9_out, or_5_out, or_3_out);
  and and_10 (and_10_out, and_8_out, decode_1_lda);
  assign controlled_buffer_10_out = and_10_out ? out_14 : 8'bz;  // Controlled_Buffer controlled_buffer_10
  assign controlled_buffer_10_out = and_13_out ? out_15 : 8'bz;  // Controlled_Buffer controlled_buffer_11
  and and_11 (and_11_out, decode_1_jz, ALU_zero);
  and and_12 (and_12_out, decode_1_jc, ALU_carry);
  assign controlled_inverter_1_out = decode_1_add ? ~decode_1_add : 1'bz;  // Controlled_Inverter controlled_inverter_1
  assign controlled_inverter_2_out = decode_1_add ? ~decode_1_add : 1'bz;  // Controlled_Inverter controlled_inverter_2
  assign controlled_inverter_1_out = decode_1_sub ? decode_1_sub : 1'bz;  // Controlled_Buffer controlled_buffer_12
  assign controlled_inverter_2_out = decode_1_sub ? ~decode_1_sub : 1'bz;  // Controlled_Inverter controlled_inverter_3
  or or_6 (or_6_out, decode_1_sub, decode_1_add);
  and and_13 (and_13_out, and_8_out, or_6_out);
  Register_8bit Register_A (.EN(and_9_out), .CLK(and_1_out), .D(controlled_buffer_10_out), .Result(out_12));
  assign controlled_buffer_13_out = and_13_out ? out_14 : 8'bz;  // Controlled_Buffer controlled_buffer_13
  assign controlled_buffer_13_out = not_8_out ? {8{1'b0}} : 8'bz;  // Controlled_Buffer controlled_buffer_14
  not not_8 (not_8_out, and_13_out);
  or or_7 (or_7_out, decode_1_add, decode_1_sub);
  not not_9 (not_9_out, or_7_out);
  assign controlled_inverter_1_out = not_9_out ? Default0 : 1'bz;  // Controlled_Buffer controlled_buffer_15
  assign controlled_inverter_2_out = not_9_out ? Default1 : 1'bz;  // Controlled_Buffer controlled_buffer_16
  The8BitAdderWithModes ALU (
    .A(out_12), .B(controlled_buffer_13_out), .EN(and_13_out), .CLK(and_1_out),
    .S0(controlled_inverter_1_out), .S1(controlled_inverter_2_out), .Carry(ALU_carry), .Zero(ALU_zero),
    .Result(out_15));

  assign out_16 = out_12;

  // Notes on the sheet:
  //   contents of rom_1 (hex, n*v repeats v):
  //   10 41 65 13 e0 12 e0
endmodule

module Simple_3bit_adder_SM (
  input  [2:0] A,
  input  [2:0] B,
  output [2:0] Result
);

  wire firstbit_1_cout, otherbit_1_cout;

  FirstBit firstbit_1 (
    .A(A[0]), .B(B[0]), .Mode(1'b0), .Sum(Result[0]), .Cout(firstbit_1_cout));  // open: OR_Out, AND_Out
  OtherBit otherbit_1 (
    .A(A[1]), .B(B[1]), .Mode(1'b0), .Cin(firstbit_1_cout), .Sum(Result[1]), .Cout(otherbit_1_cout));  // open: AND_Out, OR_Out
  OtherBit otherbit_2 (
    .A(A[2]), .B(B[2]), .Mode(1'b0), .Cin(otherbit_1_cout), .Sum(Result[2]));  // open: AND_Out, OR_Out, Cout
endmodule

module Register_7bit (
  input  EN,
  input  CLK,
  input  [6:0] D,
  output [6:0] Result
);

  Register_1bit register_1bit_1 (.D(D[0]), .En(EN), .CLK(CLK), .Q(Result[0]));
  Register_1bit register_1bit_2 (.D(D[1]), .En(EN), .CLK(CLK), .Q(Result[1]));
  Register_1bit register_1bit_3 (.D(D[2]), .En(EN), .CLK(CLK), .Q(Result[2]));
  Register_1bit register_1bit_4 (.D(D[3]), .En(EN), .CLK(CLK), .Q(Result[3]));
  Register_1bit register_1bit_5 (.D(D[4]), .En(EN), .CLK(CLK), .Q(Result[4]));
  Register_1bit register_1bit_6 (.D(D[5]), .En(EN), .CLK(CLK), .Q(Result[5]));
  Register_1bit register_1bit_7 (.D(D[6]), .En(EN), .CLK(CLK), .Q(Result[6]));
endmodule

module Register_3Bit (
  input  CLK,
  input  En,
  input  [2:0] D,
  output [2:0] State
);

  Register_1bit register_1bit_1 (.D(D[0]), .En(En), .CLK(CLK), .Q(State[0]));
  Register_1bit register_1bit_2 (.D(D[1]), .En(En), .CLK(CLK), .Q(State[1]));
  Register_1bit register_1bit_3 (.D(D[2]), .En(En), .CLK(CLK), .Q(State[2]));
endmodule
